# Fritzing sketch printer (saved by Fritzing 0.7.4b)
breadboards: 1

parts:
  Arduino_Ethernet_Shield1 = Arduino Ethernet Shield
  Ready_LED = LED - 5mm [color="Green (570nm)" package="5 mm [THT]"]
  Downloading_LED = LED - 5mm [color="Yellow (595nm)" package="5 mm [THT]"]
  Error_LED = LED - 5mm [color="Red (633nm)" package="5 mm [THT]"]
  Data = male pin header, 3 pins [form="♂ (male)"]
  Power = male pin header, 2 pins [form="♂ (male)"]
  S1 = Pushbutton [package="[THT]"]
  Rswitch = Resistor [tolerance=±5% resistance=560 package=THT]
  Ramber = Resistor [tolerance=±5% resistance=560 package=THT]
  Rgreen = Resistor [tolerance=±5% resistance=560 package=THT]
  Rred = Resistor [tolerance=±5% resistance=560 package=THT]
  Part1 = Thermal Printer

nets:
  GND: Arduino_Ethernet_Shield1.GND, Data.pin3, Power.pin2, Rswitch.Pin_1, Ramber.Pin_0, Rgreen.Pin_0, Rred.Pin_0, Part1.GND
  N1: Arduino_Ethernet_Shield1.D9, Data.pin2, Part1.RXD
  N2: Arduino_Ethernet_Shield1.D8, Data.pin1, Part1.TXD
  N3: Arduino_Ethernet_Shield1.D7, Error_LED.anode
  N4: Arduino_Ethernet_Shield1.D6, Downloading_LED.anode
  N5: Arduino_Ethernet_Shield1.D5, Ready_LED.anode
  N6: Arduino_Ethernet_Shield1.D3, S1.Pin_1, S1.Pin_2, Rswitch.Pin_0
  N7: Arduino_Ethernet_Shield1.+5V, S1.Pin_3, S1.Pin_4
  N8: Arduino_Ethernet_Shield1.VIN, Power.pin1, Part1.VH
  N9: Ready_LED.cathode, Rgreen.Pin_1
  N10: Downloading_LED.cathode, Ramber.Pin_1
  N11: Error_LED.cathode, Rred.Pin_1
